# Fritzing sketch PTC2(7segment) (saved by Fritzing 0.9.4)

parts:
  U1 = ESP32-38PinWide [part_number=ESP32-38PinWide]
  S1 = Pushbutton [package="[THT]"]
  4_Segment_-TM1637 = TM1637
  LED1 = smd LED [color="Green (560nm)" package="1206 [SMD]"]
  R1 = Resistor [tolerance=±5% resistance=220 package=THT]
  R2 = Resistor [tolerance=±5% resistance=220 package=THT]
  U2 = ESP32-38PinWide [part_number=ESP32-38PinWide]
  R3 = Resistor [tolerance=±5% resistance=220 package=THT]
  R4 = Resistor [tolerance=±5% resistance=220 package=THT]
  4_Segment_-TM1638 = TM1637
  U3 = ESP32-38PinWide [part_number=ESP32-38PinWide]
  S2 = Pushbutton [package="[THT]"]
  LED2 = smd LED [color="Green (560nm)" package="1206 [SMD]"]
  Part1 = Arduino Uno (Rev3)

nets:
  N1: U1.GND, S1.Pin_3, LED1.cathode
  N2: U1.GPIO13, R2.Pin_0
  N3: U1.GPIO9, R1.Pin_1
  N4: U1.GPIO11, 4_Segment_-TM1637.VCC
  VIN: U1.VIN, 4_Segment_-TM1637.GND
  N5: U1.GPIO15, 4_Segment_-TM1637.CLK
  N6: U1.GPIO2, 4_Segment_-TM1637.DIO
  N7: S1.Pin_2, R1.Pin_0
  N8: LED1.anode, R2.Pin_1
  N9: U2.GPIO11, Part1.GND
  VIN_2: U2.VIN, Part1.5V
  N10: U2.GPIO3, Part1.D0/RX
  N11: U2.GPIO1, Part1.D1/TX
  N12: R3.Pin_0, U3.GPIO13
  N13: R3.Pin_1, LED2.anode
  N14: R4.Pin_0, S2.Pin_2
  N15: R4.Pin_1, U3.GPIO9
  GND: 4_Segment_-TM1638.GND, U3.VIN
  N16: 4_Segment_-TM1638.VCC, U3.GPIO11
  N17: 4_Segment_-TM1638.DIO, U3.GPIO2
  N18: 4_Segment_-TM1638.CLK, U3.GPIO15
  N19: U3.GND, S2.Pin_3, LED2.cathode

notes:
  4-segment TM1637 - RM4.90
  ESP32 - RM27.26
  PB - RM0.40
  LED - RM0.10
  MASTER
  SLAVE 1
  SLAVE 2

custom parts:
  ESP32-38PinWide: Generic 38-Pin ESP32 with wide format (only access to one side of pins on a breadboard) based on Stephen Lilley's HiLetgo ESP-WROOM-32 ESP32 ESP-32S Development Board.
  TM1637: A 4 7-seg display
