# Fritzing sketch PTC2 (saved by Fritzing 0.9.4)

parts:
  U1 = ESP32-38PinWide [part_number=ESP32-38PinWide]
  Part1 = LCD1602-I2C
  S1 = Pushbutton [package="[THT]"]
  LED1 = smd LED [color="Green (560nm)" package="0805 [SMD]"]

nets:
  N1: U1.GPIO13, LED1.anode
  N2: U1.GPIO9, S1.Pin_1, S1.Pin_2
  N3: U1.GPIO11, Part1.GND
  VIN: U1.VIN, Part1.VCC
  N4: U1.GND, S1.Pin_3, LED1.cathode
  N5: U1.GPIO21, Part1.SDA
  N6: U1.GPIO22, Part1.SCL

notes:
  LCD I2C - RM14.10
  ESP32 - RM27.26
  PB - RM0.40
  LED - RM0.10

custom parts:
  ESP32-38PinWide: Generic 38-Pin ESP32 with wide format (only access to one side of pins on a breadboard) based on Stephen Lilley's HiLetgo ESP-WROOM-32 ESP32 ESP-32S Development Board.
  LCD1602-I2C: A standard character display, usually with 2x16 characters. Comes in many colors with LCM1602 IIC attached.
